# Fritzing sketch i2c_lcd_mini_v1.7 (saved by Fritzing 0.8.0b)
breadboards: 1

parts:
  pnp = PNP-Transistor [package="SOT-23 [SMD]"]
  SCL = Generic male header - 4 pins [form="♂ (male)" package=THT]
  I²C-TLCD = Generic rounded female header - 16 pins [form="♀ (female rounded)" package=THT]
  R2 = Resistor [tolerance=±5% resistance=220 package="0603 [SMD]"]
  J4 = male pin header, 3 pins [form="♂ (male)"]
  TR1 = male pin header, 1 pin [form="♂ (male)"]
  J5 = female pin header, 1 pin [form="♀ (female)"]
  IC1 = PCF8574_SO16W [chip_label=PCF8574 package=SO16W]
  J7 = female pin header, 1 pin [form="♀ (female)"]
  SDA = Generic male header - 4 pins [form="♂ (male)" package=THT]
  R77 = Resistor [tolerance=±5% resistance=0 package="1206 [SMD]"]
  A0 = Resistor [tolerance=±5% resistance=100M package="1206 [SMD]"]
  R81 = Resistor [tolerance=±5% resistance=0 package="1206 [SMD]"]
  A1 = Resistor [tolerance=±5% resistance=100M package="1206 [SMD]"]
  R76 = Resistor [tolerance=±5% resistance=0 package="1206 [SMD]"]
  A2 = Resistor [tolerance=±5% resistance=100M package="1206 [SMD]"]
  J8 = male pin header, 2 pins [form="♂ (male)"]

nets:
  5V: pnp.2, SCL.5V, I²C-TLCD.Vdd, J4.pin1, IC1.5V, J7.pin1, SDA.5V, A0.Pin_1, A1.Pin_1, A2.Pin_1, J8.pin1, J8.pin2
  N1: pnp.0, R2.Pin_1
  N2: pnp.1, I²C-TLCD.LED+
  N3: SCL.SDA, IC1.SDA, SDA.SDA
  N4: SCL.SCL, IC1.SCL, SDA.SCL
  GND: SCL.GND, I²C-TLCD.Vss, I²C-TLCD.D0, I²C-TLCD.D1, I²C-TLCD.D2, I²C-TLCD.D3, I²C-TLCD.LED-, J4.pin3, IC1.GND, SDA.GND, R77.Pin_1, R81.Pin_1, R76.Pin_1
  N5: I²C-TLCD.V0, J4.pin2, TR1.pin1, J5.pin1
  N6: I²C-TLCD.RS, IC1.P4
  N7: I²C-TLCD.R/W, IC1.P5
  N8: I²C-TLCD.E1, IC1.P6
  N9: I²C-TLCD.D4, IC1.P0
  N10: I²C-TLCD.D5, IC1.P1
  N11: I²C-TLCD.D6, IC1.P2
  N12: I²C-TLCD.D7, IC1.P3
  N13: R2.Pin_0, IC1.P7
  N14: IC1.A0, R77.Pin_0, A0.Pin_0
  N15: IC1.A1, R81.Pin_0, A1.Pin_0
  N16: IC1.A2, R76.Pin_0, A2.Pin_0

notes:
  0
  1
  16
  5V
  GND
  SDA
  SCL
  I2C-TLCD
  2  1  0
  I2C-Addr
  PCF8574

custom parts:
  Generic male header - 4 pins: Generic male header
  Generic rounded female header - 16 pins: Generic rounded female header
